// Digital circuit 4-bit-DRAM-with-registers.dig as structural Verilog
module _4_bit_DRAM_with_registers (
  input  clk,
  input  [1:0] ctrl__Load__Store__Reset,
  input  [1:0] ctrl_IR__Load__Store__Reset,
  input  [1:0] ctrl_PC__Load__INC__Reset,
  input  [3:0] Input_Mem,
  input  PC,
  input  [1:0] Address,
  output [3:0] out_6
);

  wire [1:0] multiplexer_1_out, programcounter_1_x;
  wire [3:0] general_purpose_register_1_output;
  wire [3:2] programcounter_1_x_2;

  Multiplexer #(.Bits(2)) multiplexer_1 (.sel(PC), .in_0(programcounter_1_x), .in_1(Address), .out(multiplexer_1_out));
  General_Purpose_Register general_purpose_register_1 (
    .Address(multiplexer_1_out), .Input(Input_Mem), .CTRL(ctrl__Load__Store__Reset), .Clock(clk),
    .Output(general_purpose_register_1_output));
  ProgramCounter programcounter_1 (
    .CTRL(ctrl_PC__Load__INC__Reset), .CLK(clk), .X({programcounter_1_x_2, programcounter_1_x}));
  _4_bit_instruction_register _4_bit_instruction_register_1 (
    .clk(clk), .CTRL(ctrl_IR__Load__Store__Reset), .Input(general_purpose_register_1_output), .Output(out_6));
endmodule
