// Digital circuit 4-bit-Dram-with-registers.dig as structural Verilog
module _4_bit_Dram_with_registers (
  input  clk,
  input  [1:0] ctrl__Load__Store__Reset,
  input  [1:0] ctrl_IR__Load__Store__Reset,
  input  [1:0] ctrl_PC__Load__INC__Reset,
  input  [3:0] Input_Mem,
  input  PC_On_Off,
  input  [3:0] Address,
  output [3:0] Output,
  output Overflow
);

  wire [3:0] _4_bit_16_address_dram_1_p5, multiplexer_1_out, programcounter_1_x;

  Multiplexer #(.Bits(4)) multiplexer_1 (
    .sel(PC_On_Off), .in_0(programcounter_1_x), .in_1(Address), .out(multiplexer_1_out));
  // _4_bit_16_address_Dram _4_bit_16_address_dram_1: pin names not known; wires that end beside it: multiplexer_1_out, Input_Mem, ctrl__Load__Store__Reset, clk, _4_bit_16_address_dram_1_p5
  ProgramCounter programcounter_1 (
    .CTRL(ctrl_PC__Load__INC__Reset), .CLK(clk), .X(programcounter_1_x), .Overflow(Overflow));
  _4_bit_instruction_register _4_bit_instruction_register_1 (
    .clk(clk), .CTRL(ctrl_IR__Load__Store__Reset), .Input(_4_bit_16_address_dram_1_p5), .Output(Output));
endmodule
