// Digital circuit 4-bit_Adder.dig as structural Verilog
module _4_bit_Adder (
  input  [3:0] A,
  input  [3:0] B,
  output [3:0] Sum,
  output Overflow_flag
);

  wire adder_1_p3, adder_2_p3, adder_3_p3;

  // Adder adder_1: pin names not known; wires that end beside it: A[3], B[3], adder_1_p3, Sum[3], Overflow_flag
  // Adder adder_2: pin names not known; wires that end beside it: A[2], B[2], adder_2_p3, Sum[2], adder_1_p3
  // Adder adder_3: pin names not known; wires that end beside it: A[1], B[1], adder_3_p3, Sum[1], adder_2_p3
  // Adder adder_4: pin names not known; wires that end beside it: A[0], B[0], 1'b0, Sum[0], adder_3_p3
endmodule
