// Digital circuit General_Purpose_Register.dig as structural Verilog
module General_Purpose_Register (
  input  [1:0] Address,
  input  [3:0] Input,
  input  [1:0] CTRL,
  input  Clock,
  output [3:0] Output
);

  wire and_1_out, and_2_out, and_3_out, and_4_out, decoder_1_out_0, decoder_1_out_1, decoder_1_out_2,
       decoder_1_out_3;
  wire [3:0] _4_bit_register_1_y, _4_bit_register_2_y, _4_bit_register_3_y, _4_bit_register_4_y;

  Decoder #(.Selector_Bits(2)) decoder_1 (
    .sel(Address), .out_0(decoder_1_out_0), .out_1(decoder_1_out_1), .out_2(decoder_1_out_2),
    .out_3(decoder_1_out_3));
  and and_1 (and_1_out, Clock, decoder_1_out_0);
  and and_2 (and_2_out, Clock, decoder_1_out_1);
  and and_3 (and_3_out, Clock, decoder_1_out_2);
  and and_4 (and_4_out, Clock, decoder_1_out_3);
  _4_bit_register _4_bit_register_1 (.X(Input), .CTRL(CTRL), .Clock(and_1_out), .Y(_4_bit_register_1_y));
  _4_bit_register _4_bit_register_2 (.X(Input), .CTRL(CTRL), .Clock(and_2_out), .Y(_4_bit_register_2_y));
  _4_bit_register _4_bit_register_3 (.X(Input), .CTRL(CTRL), .Clock(and_3_out), .Y(_4_bit_register_3_y));
  _4_bit_register _4_bit_register_4 (.X(Input), .CTRL(CTRL), .Clock(and_4_out), .Y(_4_bit_register_4_y));
  Multiplexer #(.Bits(4), .Selector_Bits(2)) multiplexer_1 (
    .sel(Address), .in_0(_4_bit_register_1_y), .in_1(_4_bit_register_2_y), .in_2(_4_bit_register_3_y),
    .in_3(_4_bit_register_4_y), .out(Output));
endmodule
